// Digital circuit 16x4bitMEM.dig as structural Verilog
module _16x4bitMEM (
  input  [3:0] A,
  input  [3:0] D_in,
  input  In,
  output [3:0] D_out,
  output [3:0] A_out
);

  wire demultiplexer_1_out_0, demultiplexer_1_out_1, demultiplexer_1_out_2, demultiplexer_1_out_3,
       demultiplexer_1_out_4, demultiplexer_1_out_5, demultiplexer_1_out_6, demultiplexer_1_out_7,
       demultiplexer_1_out_8, demultiplexer_1_out_9, demultiplexer_1_out_10, demultiplexer_1_out_11,
       demultiplexer_1_out_12, demultiplexer_1_out_13, demultiplexer_1_out_14, demultiplexer_1_out_15;
  wire [3:0] M0_d_out, M1_d_out, M2_d_out, M3_d_out, M4_d_out, M5_d_out, M6_d_out, M7_d_out, M8_d_out,
       M9_d_out, M10_d_out, M11_d_out, M12_d_out, M13_d_out, M14_d_out, M15_d_out;

  Demultiplexer #(.Selector_Bits(4)) demultiplexer_1 (
    .sel(A), .in(In), .out_0(demultiplexer_1_out_0), .out_1(demultiplexer_1_out_1),
    .out_2(demultiplexer_1_out_2), .out_3(demultiplexer_1_out_3), .out_4(demultiplexer_1_out_4),
    .out_5(demultiplexer_1_out_5), .out_6(demultiplexer_1_out_6), .out_7(demultiplexer_1_out_7),
    .out_8(demultiplexer_1_out_8), .out_9(demultiplexer_1_out_9), .out_10(demultiplexer_1_out_10),
    .out_11(demultiplexer_1_out_11), .out_12(demultiplexer_1_out_12), .out_13(demultiplexer_1_out_13),
    .out_14(demultiplexer_1_out_14), .out_15(demultiplexer_1_out_15));
  _4bit_memory M0 (.D_in(D_in), .Write(demultiplexer_1_out_0), .D_out(M0_d_out));
  _4bit_memory M1 (.D_in(D_in), .Write(demultiplexer_1_out_1), .D_out(M1_d_out));
  _4bit_memory M2 (.D_in(D_in), .Write(demultiplexer_1_out_2), .D_out(M2_d_out));
  _4bit_memory M3 (.D_in(D_in), .Write(demultiplexer_1_out_3), .D_out(M3_d_out));
  _4bit_memory M4 (.D_in(D_in), .Write(demultiplexer_1_out_4), .D_out(M4_d_out));
  _4bit_memory M5 (.D_in(D_in), .Write(demultiplexer_1_out_5), .D_out(M5_d_out));
  _4bit_memory M6 (.D_in(D_in), .Write(demultiplexer_1_out_6), .D_out(M6_d_out));
  _4bit_memory M7 (.D_in(D_in), .Write(demultiplexer_1_out_7), .D_out(M7_d_out));
  _4bit_memory M8 (.D_in(D_in), .Write(demultiplexer_1_out_8), .D_out(M8_d_out));
  _4bit_memory M9 (.D_in(D_in), .Write(demultiplexer_1_out_9), .D_out(M9_d_out));
  _4bit_memory M10 (.D_in(D_in), .Write(demultiplexer_1_out_10), .D_out(M10_d_out));
  _4bit_memory M11 (.D_in(D_in), .Write(demultiplexer_1_out_11), .D_out(M11_d_out));
  _4bit_memory M12 (.D_in(D_in), .Write(demultiplexer_1_out_12), .D_out(M12_d_out));
  _4bit_memory M13 (.D_in(D_in), .Write(demultiplexer_1_out_13), .D_out(M13_d_out));
  _4bit_memory M14 (.D_in(D_in), .Write(demultiplexer_1_out_14), .D_out(M14_d_out));
  _4bit_memory M15 (.D_in(D_in), .Write(demultiplexer_1_out_15), .D_out(M15_d_out));
  Multiplexer #(.Selector_Bits(4), .Bits(4)) multiplexer_1 (
    .sel(A), .in_0(M0_d_out), .in_1(M1_d_out), .in_2(M2_d_out), .in_3(M3_d_out), .in_4(M4_d_out),
    .in_5(M5_d_out), .in_6(M6_d_out), .in_7(M7_d_out), .in_8(M8_d_out), .in_9(M9_d_out), .in_10(M10_d_out),
    .in_11(M11_d_out), .in_12(M12_d_out), .in_13(M13_d_out), .in_14(M14_d_out), .in_15(M15_d_out), .out(D_out));

  assign A_out = A;
endmodule
