// Digital circuit 4bit_Incrementor.dig as structural Verilog
module _4bit_Incrementor (
  input  [3:0] A,
  output Cout,
  output [3:0] S
);

  wire and_1_out, and_2_out, and_3_out;

  xor xor_1 (S[0], 1'b1, A[0]);
  and and_1 (and_1_out, 1'b1, A[0]);
  xor xor_2 (S[1], and_1_out, A[1]);
  and and_2 (and_2_out, and_1_out, A[1]);
  xor xor_3 (S[2], and_2_out, A[2]);
  and and_3 (and_3_out, and_2_out, A[2]);
  xor xor_4 (S[3], and_3_out, A[3]);
  and and_4 (Cout, and_3_out, A[3]);
endmodule
