// Digital circuit 4bit_PC.dig as structural Verilog
module _4bit_PC (
  input  [3:0] D,
  input  Clock,
  input  Sel,
  input  [1:0] Control,
  output [3:0] Q_plus_1
);

  wire [3:0] multiplexer_1_out, PC_q;

  Multiplexer #(.Bits(4)) multiplexer_1 (.sel(Sel), .in_0(Q_plus_1), .in_1(D), .out(multiplexer_1_out));
  _4bit_Register PC (.Clock(Clock), .D(multiplexer_1_out), .Control(Control), .Q(PC_q));
  _4bit_Incrementor INC (.A(PC_q), .S(Q_plus_1));  // open: Cout
endmodule
