// Digital circuit 4bit_memory.dig as structural Verilog
module _4bit_memory (
  input  [3:0] D_in,
  input  Write,
  output [3:0] D_out
);

  D_latch d_latch_1 (.D_in(D_in[0]), .E(Write), .Q(D_out[0]));
  D_latch d_latch_2 (.D_in(D_in[1]), .E(Write), .Q(D_out[1]));
  D_latch d_latch_3 (.D_in(D_in[2]), .E(Write), .Q(D_out[2]));
  D_latch d_latch_4 (.D_in(D_in[3]), .E(Write), .Q(D_out[3]));
endmodule
