// Digital circuit D-latch.dig as structural Verilog
module D_latch (
  input  D_in,
  input  E,
  output Q
);

  wire and_1_out, and_2_out, nor_2_out, not_1_out;

  not not_1 (not_1_out, D_in);
  and and_1 (and_1_out, E, D_in);
  and and_2 (and_2_out, not_1_out, E);
  nor nor_1 (Q, and_2_out, nor_2_out);
  nor nor_2 (nor_2_out, Q, and_1_out);
endmodule
