// Digital circuit IR.dig as structural Verilog
module IR (
  input  clk,
  input  [1:0] Control,
  input  [1:0] Control_2,
  input  Sel,
  input  [3:0] D_in,
  input  In,
  output [3:0] IR_out
);

  wire [3:0] _4bit_pc_1_q_plus_1, _16x4bitmem_1_a_out, _16x4bitmem_1_d_out;

  _4bit_PC _4bit_pc_1 (
    .D(_16x4bitmem_1_a_out), .Clock(clk), .Sel(Sel), .Control(Control), .Q_plus_1(_4bit_pc_1_q_plus_1));
  _16x4bitMEM _16x4bitmem_1 (
    .A(_4bit_pc_1_q_plus_1), .D_in(D_in), .In(In), .D_out(_16x4bitmem_1_d_out), .A_out(_16x4bitmem_1_a_out));
  _4bit_Register IR (.Clock(clk), .D(_16x4bitmem_1_d_out), .Control(Control_2), .Q(IR_out));
endmodule
