// Digital circuit RAM.dig as structural Verilog
module RAM (
  input  [3:0] A,
  input  [3:0] Data_in,
  input  Clk,
  input  [1:0] Control,
  output [3:0] Data_out
);

  wire [3:0] _16x4bitmem_1_a_out, d_flip_flop_1_p3, d_flip_flop_2_p3, driver_1_out;

  assign driver_1_out = Control[1] ? Data_in : 4'bz;  // Driver driver_1
  // D_flip_flop d_flip_flop_1: pin names not known; wires that end beside it: A, Clk, d_flip_flop_1_p3
  // D_flip_flop d_flip_flop_2: pin names not known; wires that end beside it: driver_1_out, Clk, d_flip_flop_2_p3
  _16x4bitMEM _16x4bitmem_1 (
    .A(d_flip_flop_1_p3), .D_in(d_flip_flop_2_p3), .In(Control[1]), .A_out(_16x4bitmem_1_a_out));  // open: D_out
  assign Data_out = Control[0] ? _16x4bitmem_1_a_out : 4'bz;  // Driver driver_2
endmodule
