// Digital circuit Register_File.dig as structural Verilog
module Register_File (
  input  [3:0] Read_Register_1,
  input  [3:0] Read_Register_2,
  input  [1:0] Write_Register,
  input  [3:0] Write_Data,
  input  Clock,
  input  [1:0] Control,
  output [3:0] Read_Data_1,
  output [3:0] Read_Data_2
);

  wire [3:0] A_q, B_q, D_q, demultiplexer_1_out_0, demultiplexer_1_out_1, demultiplexer_1_out_2,
       demultiplexer_1_out_3, IR_q;

  Demultiplexer #(.Selector_Bits(2), .Bits(4)) demultiplexer_1 (
    .sel(Write_Register), .in(Write_Data), .out_0(demultiplexer_1_out_0), .out_1(demultiplexer_1_out_1),
    .out_2(demultiplexer_1_out_2), .out_3(demultiplexer_1_out_3));
  _4bit_Register A (.Clock(Clock), .D(demultiplexer_1_out_0), .Control(Control), .Q(A_q));
  _4bit_Register B (.Clock(Clock), .D(demultiplexer_1_out_1), .Control(Control), .Q(B_q));
  _4bit_Register IR (.Clock(Clock), .D(demultiplexer_1_out_2), .Control(Control), .Q(IR_q));
  _4bit_Register D (.Clock(Clock), .D(demultiplexer_1_out_3), .Control(Control), .Q(D_q));
  Multiplexer #(.Selector_Bits(2), .Bits(4)) multiplexer_1 (
    .sel(Read_Register_1[1:0]), .in_0(A_q), .in_1(B_q), .in_2(IR_q), .in_3(D_q), .out(Read_Data_1));
  Multiplexer #(.Selector_Bits(2), .Bits(4)) multiplexer_2 (
    .sel(Read_Register_2[1:0]), .in_0(A_q), .in_1(B_q), .in_2(IR_q), .in_3(D_q), .out(Read_Data_2));
  // Pins of 2 and 4 bits meet at Read_Register_1
  // Pins of 2 and 4 bits meet at Read_Register_2
  // Pins of 1 and 2 bits meet at Write_Register
  // Pins of 1 and 4 bits meet at Write_Data
endmodule
